# Fritzing sketch proto_io-exp (saved by Fritzing 0.9.2b)
circuit board: 6.87654cm x 5.3026cm
breadboards: 1

parts:
  R33 = Resistor [tolerance=±5% resistance=220 package=THT]
  MCP23017 = IC, DIP package, 28 pins [chip_label=IC part_number=MCP23017]
  ULN2003A = ULN2003A [package="DIP16 [THT]"]
  DS18030-010+1 = IC, DIP package, 16 pins [chip_label=IC]
  ILQ6 = IC, DIP package, 16 pins [chip_label=IC]
  R34 = Resistor [tolerance=±5% resistance=220 package=THT]
  R35 = Resistor [tolerance=±5% resistance=10k package=THT]
  R36 = Resistor [tolerance=±5% resistance=10k package=THT]
  R37 = Resistor [tolerance=±5% resistance=10k package=THT]
  R38 = Resistor [tolerance=±5% resistance=1k package=THT]
  R39 = Resistor [tolerance=±5% resistance=1k package=THT]
  R40 = Resistor [tolerance=±5% resistance=1k package=THT]
  R41 = Resistor [tolerance=±5% resistance=1k package=THT]
  R42 = Resistor [tolerance=±5% resistance=10k package=THT]
  C30 = Electrolytic Capacitor [capacitance=10µF package="100 mil [THT, electrolytic]"]
  C31 = Electrolytic Capacitor [capacitance=10µF package="100 mil [THT, electrolytic]"]
  J6 = double row female pin header, 10 pins [form="♀ (female)"]
  R44 = Resistor [tolerance=±5% resistance=4.7k package=THT]
  R45 = Resistor [tolerance=±5% resistance=4.7k package=THT]
  R46 = Resistor [tolerance=±5% resistance=1k package=THT]
  R48 = Resistor [tolerance=±5% resistance=10k package=THT]
  Q-P = double row female pin header, 6 pins [form="♀ (female)"]
  DS18030-010+2 = IC, DIP package, 16 pins [chip_label=IC]
  S-R = double row female pin header, 6 pins [form="♀ (female)"]
  IC7 = SO08 [chip_label=IC part_number=DS2482-100 package=SO]
  I-S1 = molex pin header, 3 pins [form=molex]
  -_O_E_F_A_- = molex pin header, 6 pins [form=molex]
  J7 = molex pin header, 8 pins [form=molex]
  R49 = Resistor [tolerance=±5% resistance=1k package=THT]
  R50 = Resistor [tolerance=±5% resistance=1k package=THT]
  I-S = molex pin header, 5 pins [form=molex]
  J10 = double row female pin header, 2 pins [form="♀ (female)"]
  C32 = Electrolytic Capacitor [capacitance=1mF voltage=35V package="100 mil [THT, electrolytic]"]
  C34 = Ceramic Capacitor [capacitance=100nF package="100 mil [THT, multilayer]"]
  Componente1 = Arduino Leonardo (Rev3b)

nets:
  N1: R33.Pin_0, R36.Pin_1, R42.Pin_0, C31.+, I-S.pin1
  N2: R33.Pin_1, I-S.pin2, Componente1.A0
  N3: MCP23017.pin1, R39.Pin_0
  N4: MCP23017.pin2, ULN2003A.In_7
  N5: MCP23017.pin3, ULN2003A.In_6
  N6: MCP23017.pin4, ULN2003A.In_5
  N7: MCP23017.pin5, ULN2003A.In_4
  N8: MCP23017.pin6, ULN2003A.In_3
  N9: MCP23017.pin7, ULN2003A.In_2
  N10: MCP23017.pin8, ULN2003A.In_1
  5V: MCP23017.pin9, MCP23017.pin15, DS18030-010+1.pin5, DS18030-010+1.pin16, R37.Pin_1, R42.Pin_1, R44.Pin_1, R45.Pin_1, R46.Pin_1, R48.Pin_0, DS18030-010+2.pin5, DS18030-010+2.pin6, DS18030-010+2.pin16, IC7.1, I-S1.pin3, R49.Pin_1, R50.Pin_1, Componente1.5V
  GND: MCP23017.pin10, MCP23017.pin16, MCP23017.pin17, ULN2003A.0V, DS18030-010+1.pin6, DS18030-010+1.pin7, DS18030-010+1.pin8, ILQ6.pin2, ILQ6.pin3, ILQ6.pin6, ILQ6.pin7, R35.Pin_0, R36.Pin_0, C30.-, C31.-, J6.pin6, J6.pin7, J6.pin8, J6.pin9, J6.pin10, DS18030-010+2.pin7, DS18030-010+2.pin8, IC7.3, IC7.7, IC7.8, I-S1.pin1, I-S.pin3, C32.-, C34.1, Componente1.GND
  N11: MCP23017.pin12, DS18030-010+1.pin9, R44.Pin_0, DS18030-010+2.pin9, IC7.4, Componente1.D3_PWM/SCL, Componente1.SCL
  N12: MCP23017.pin13, DS18030-010+1.pin10, R45.Pin_0, DS18030-010+2.pin10, IC7.5, Componente1.D2/SDA, Componente1.SDA
  N13: MCP23017.pin18, R48.Pin_1
  N14: MCP23017.pin19, J10.pin2
  N15: MCP23017.pin20, J10.pin1
  N16: MCP23017.pin21, R40.Pin_0
  N17: MCP23017.pin22, R41.Pin_0
  N18: MCP23017.pin23, R38.Pin_0
  N19: MCP23017.pin24, J6.pin5
  N20: MCP23017.pin25, J6.pin4
  N21: MCP23017.pin26, J6.pin3
  N22: MCP23017.pin27, J6.pin2
  N23: MCP23017.pin28, J6.pin1
  N24: ULN2003A.COM_-_Common, J7.pin1, C32.+, C34.0
  N25: ULN2003A.Out_7, J7.pin2
  N26: ULN2003A.Out_6, J7.pin3
  N27: ULN2003A.Out_5, J7.pin4
  N28: ULN2003A.Out_4, J7.pin5
  N29: ULN2003A.Out_3, J7.pin6
  N30: ULN2003A.Out_2, J7.pin7
  N31: ULN2003A.Out_1, J7.pin8
  N32: DS18030-010+1.pin1, Q-P.pin5, Q-P.pin6
  N33: DS18030-010+1.pin3, DS18030-010+1.pin4, Q-P.pin1, Q-P.pin2
  N34: DS18030-010+1.pin12, DS18030-010+1.pin13, Q-P.pin4
  N35: DS18030-010+1.pin14, Q-P.pin3
  N36: ILQ6.pin1, R39.Pin_1
  N37: ILQ6.pin4, R40.Pin_1
  N38: ILQ6.pin5, R41.Pin_1
  N39: ILQ6.pin8, R38.Pin_1
  N40: ILQ6.pin9, ILQ6.pin12, -_O_E_F_A_-.pin1
  N41: ILQ6.pin10, -_O_E_F_A_-.pin2
  N42: ILQ6.pin11, -_O_E_F_A_-.pin3
  N43: ILQ6.pin13, ILQ6.pin16, -_O_E_F_A_-.pin6
  N44: ILQ6.pin14, -_O_E_F_A_-.pin4
  N45: ILQ6.pin15, -_O_E_F_A_-.pin5
  N46: R34.Pin_0, R35.Pin_1, R37.Pin_0, C30.+, I-S.pin4
  N47: R34.Pin_1, I-S.pin5, Componente1.A1
  N48: R46.Pin_0, IC7.2, I-S1.pin2
  N49: DS18030-010+2.pin1, S-R.pin5, S-R.pin6
  N50: DS18030-010+2.pin3, DS18030-010+2.pin4, S-R.pin1, S-R.pin2
  N51: DS18030-010+2.pin12, DS18030-010+2.pin13, S-R.pin4
  N52: DS18030-010+2.pin14, S-R.pin3
  N53: R49.Pin_0, Componente1.D10_PWM/A10
  N54: R50.Pin_0, Componente1.D9_PWM/A9
